# Fritzing sketch Motor-Raspberry (saved by Fritzing 0.9.3b)
breadboards: 1

parts:
  Raspberry_Pi1 = Raspberry Pi B+
  Bauteil1 = AF_mshield-v1.2_breadboard
  M4 = DC Motor
  M5 = DC Motor
  M6 = DC Motor
  M7 = DC Motor
  BAT1 = Battery Holders [package=battery-aa]

nets:
  N1: Raspberry_Pi1.GPIO5, Bauteil1.PWM0A
  N2: Raspberry_Pi1.GPIO6, Bauteil1.PWM0B
  N3: Raspberry_Pi1.GPIO13, Bauteil1.PWM2A
  N4: Raspberry_Pi1.GPIO19, Bauteil1.PWM2B
  N5: Raspberry_Pi1.GPIO21, Bauteil1.DIR_LATCH
  N6: Raspberry_Pi1.GPIO20, Bauteil1.DIR_CLK
  N7: Raspberry_Pi1.GPIO16, Bauteil1.DIR_SER
  N8: Raspberry_Pi1.GND, Bauteil1.DIR_EN
  5V: Raspberry_Pi1.5V, Bauteil1.VCC, BAT1.+
  N9: Bauteil1.1, Bauteil1.P4#174, M4.pin_2
  N10: Bauteil1.3#41, Bauteil1.P1#166, M6.pin_2
  N11: Bauteil1.6, Bauteil1.P2#167, M6.pin_1
  N12: Bauteil1.3#57, Bauteil1.P5#175, M4.pin_1
  N13: Bauteil1.11, Bauteil1.P1#171, M5.pin_2
  N14: Bauteil1.GND, BAT1.-
  N15: Bauteil1.P4#169, M7.pin_2
  N16: Bauteil1.P5#170, M7.pin_1
  N17: Bauteil1.P2#172, M5.pin_1

custom parts:
  : motor Shield v1 Adafruit Adafruit Motor/Stepper/Servo Shield for Arduino kit [v1.2] : ID 81 : $19.50 : Adafruit Industries, Unique & fun DIY electronics and kits
