# Fritzing sketch Ultraschall-Raspberry (saved by Fritzing 0.9.3b)
breadboards: 1

parts:
  Raspberry_Pi2 = Raspberry Pi B+
  hc-sr1 = hc-sr04
  hc-sr2 = hc-sr04
  hc-sr3 = hc-sr04
  hc-sr4 = hc-sr04 [part_number=Vorne]
  Bauteil1 = Arduino Nano (Rev3.0) (ICSP)
  hc-sr5 = hc-sr04

nets:
  GND: Raspberry_Pi2.GND, hc-sr1.GND, hc-sr2.GND, hc-sr3.GND, hc-sr4.GND, hc-sr5.GND
  VCC: hc-sr1.VCC, hc-sr2.VCC, hc-sr3.VCC, hc-sr4.VCC, hc-sr5.VCC
  N1: hc-sr1.Trig, Bauteil1.D7
  N2: hc-sr1.Echo, Bauteil1.D10
  N3: hc-sr2.Trig, Bauteil1.D2
  N4: hc-sr2.Echo, Bauteil1.D3
  N5: hc-sr3.Trig, Bauteil1.D4
  N6: hc-sr3.Echo, Bauteil1.D5
  N7: hc-sr4.Trig, Bauteil1.D8
  N8: hc-sr4.Echo, Bauteil1.D9
  N9: Bauteil1.D11/MOSI, hc-sr5.Echo
  N10: Bauteil1.D12/MISO, hc-sr5.Trig
